// Logisim project logic_circuit_experiment.circ as structural Verilog
module \_16進表示部品を用いた回路  (
  input  A0,
  input  A1,
  input  A2,
  input  A3
);

  Hex_Digit_Display hex_digit_display_1 (.value({A3, A2, A1, A0}));  // open: dp
endmodule

// Half Adder
module \_1ビット半加算器  (
  input  A,
  input  B,
  output C,
  output S
);

  and and_1 (C, A, B);
  xor xor_1 (S, A, B);
endmodule

// Full Adder
module \_1ビット全加算器  (
  input  A,
  input  B,
  input  C,
  output C_prime,
  output S
);

  wire \n1ビット半加算器_1_c , \n1ビット半加算器_1_s , \n1ビット半加算器_2_c ;

  \_1ビット半加算器  \u_1ビット半加算器_1  (.A(A), .C(\n1ビット半加算器_1_c ), .B(B), .S(\n1ビット半加算器_1_s ));
  \_1ビット半加算器  \u_1ビット半加算器_2  (.A(\n1ビット半加算器_1_s ), .C(\n1ビット半加算器_2_c ), .B(C), .S(S));
  or or_1 (C_prime, \n1ビット半加算器_1_c , \n1ビット半加算器_2_c );

  // Notes on the sheet:
  //   A
  //   B
  //   C
  //   S
  //   A
  //   B
  //   C
  //   S
endmodule

module \NAND回路のみを用いた半加算器と全加算器  (
  input  A,
  input  B,
  input  A_2,
  input  B_2,
  input  C,
  output C_2,
  output S,
  output C_prime,
  output S_2
);

  wire nand_1_out, nand_2_out, nand_3_out, nand_4_out, nand_5_out, nand_6_out, nand_8_out, nand_9_out,
       nand_12_out, nand_13_out;

  nand nand_1 (nand_1_out, A, B);
  nand nand_2 (nand_2_out, A_2, B_2);
  nand nand_3 (nand_3_out, A, nand_1_out);
  nand nand_4 (nand_4_out, nand_1_out, B);
  nand nand_5 (nand_5_out, A_2, nand_2_out);
  nand nand_6 (nand_6_out, nand_2_out, B_2);
  nand nand_7 (C_2, nand_1_out, nand_1_out);
  nand nand_8 (nand_8_out, nand_5_out, nand_6_out);
  nand nand_9 (nand_9_out, nand_8_out, C);
  nand nand_10 (S, nand_3_out, nand_4_out);
  nand nand_11 (C_prime, nand_2_out, nand_9_out);
  nand nand_12 (nand_12_out, nand_8_out, nand_9_out);
  nand nand_13 (nand_13_out, nand_9_out, C);
  nand nand_14 (S_2, nand_12_out, nand_13_out);

  // Notes on the sheet:
  //   Half Adder
  //   Full Adder
endmodule

module \_7入力並列カウンタ  (
  input  A_0,
  input  A_1,
  input  A_2,
  input  A_3,
  input  A_4,
  input  A_5,
  input  A_6,
  output Q_2,
  output Q_1,
  output Q_0
);

  wire \n1ビット全加算器_1_c_prime , \n1ビット全加算器_1_s , \n1ビット全加算器_3_c_prime , \n1ビット全加算器_3_s , \n1ビット全加算器_4_c_prime ;

  \_1ビット全加算器  \u_1ビット全加算器_1  (.A(A_0), .B(A_1), .C(A_2), .C_prime(\n1ビット全加算器_1_c_prime ), .S(\n1ビット全加算器_1_s ));
  \_1ビット全加算器  \u_1ビット全加算器_2  (
    .A(\n1ビット全加算器_1_c_prime ), .B(\n1ビット全加算器_3_c_prime ), .C(\n1ビット全加算器_4_c_prime ), .C_prime(Q_2), .S(Q_1));
  \_1ビット全加算器  \u_1ビット全加算器_3  (.A(A_3), .B(A_4), .C(A_5), .C_prime(\n1ビット全加算器_3_c_prime ), .S(\n1ビット全加算器_3_s ));
  \_1ビット全加算器  \u_1ビット全加算器_4  (
    .A(\n1ビット全加算器_1_s ), .B(\n1ビット全加算器_3_s ), .C(A_6), .C_prime(\n1ビット全加算器_4_c_prime ), .S(Q_0));
endmodule

// 4-bit sequential carry adder
module \_4ビット順次桁上げ加算器  (
  input  y_3,
  input  x_3,
  input  y_2,
  input  x_2,
  input  y_1,
  input  x_1,
  input  y_0,
  input  x_0,
  output O_F,
  output z_3,
  output z_2,
  output z_1,
  output z_0
);

  wire \n1ビット全加算器_2_c_prime , \n1ビット全加算器_3_c_prime , \n1ビット半加算器_1_c ;

  \_1ビット全加算器  \u_1ビット全加算器_1  (.A(y_3), .B(x_3), .C(\n1ビット全加算器_2_c_prime ), .C_prime(O_F), .S(z_3));
  \_1ビット全加算器  \u_1ビット全加算器_2  (.A(y_2), .B(x_2), .C(\n1ビット全加算器_3_c_prime ), .C_prime(\n1ビット全加算器_2_c_prime ), .S(z_2));
  \_1ビット全加算器  \u_1ビット全加算器_3  (.A(y_1), .B(x_1), .C(\n1ビット半加算器_1_c ), .C_prime(\n1ビット全加算器_3_c_prime ), .S(z_1));
  \_1ビット半加算器  \u_1ビット半加算器_1  (.A(x_0), .C(\n1ビット半加算器_1_c ), .B(y_0), .S(z_0));

  // Notes on the sheet:
  //   B
  //   S
  //   A
  //   C
endmodule

// 4-bit sign inverter
module \_4ビット符号反転器  (
  input  a_3,
  input  a_2,
  input  a_1,
  input  a_0,
  output O_F,
  output b_2,
  output b_3,
  output b_1,
  output b_0
);

  wire not_1_out, not_2_out, not_3_out, not_4_out;

  not not_1 (not_1_out, a_3);
  \_4ビット順次桁上げ加算器  \u_4ビット順次桁上げ加算器_1  (
    .y_3(not_1_out), .x_3(1'b0), .y_2(not_2_out), .x_2(1'b0), .y_1(not_3_out), .x_1(1'b0), .y_0(not_4_out),
    .x_0(1'b1), .O_F(O_F), .z_3(b_3), .z_2(b_2), .z_1(b_1), .z_0(b_0));
  not not_2 (not_2_out, a_2);
  not not_3 (not_3_out, a_1);
  not not_4 (not_4_out, a_0);
endmodule

// 4-bit parallel subtractor
module \_4ビット並列減算器  (
  input  s_3,
  input  s_2,
  input  s_1,
  input  s_0,
  input  t_3,
  input  t_2,
  input  t_1,
  input  t_0,
  output O_F__1,
  output O_F__2,
  output u_3,
  output u_2,
  output u_1,
  output u_0
);

  wire \n4ビット符号反転器_1_b_0 , \n4ビット符号反転器_1_b_1 , \n4ビット符号反転器_1_b_2 , \n4ビット符号反転器_1_b_3 ;

  \_4ビット符号反転器  \u_4ビット符号反転器_1  (
    .a_3(s_3), .a_1(s_1), .a_0(s_0), .O_F(O_F__1), .b_3(\n4ビット符号反転器_1_b_3 ), .b_2(\n4ビット符号反転器_1_b_2 ),
    .b_1(\n4ビット符号反転器_1_b_1 ), .b_0(\n4ビット符号反転器_1_b_0 ), .a_2(s_2));
  \_4ビット順次桁上げ加算器  \u_4ビット順次桁上げ加算器_1  (
    .y_3(\n4ビット符号反転器_1_b_3 ), .x_3(t_3), .y_2(\n4ビット符号反転器_1_b_2 ), .x_2(t_2), .y_1(\n4ビット符号反転器_1_b_1 ),
    .x_1(t_1), .y_0(\n4ビット符号反転器_1_b_0 ), .x_0(t_0), .O_F(O_F__2), .z_3(u_3), .z_2(u_2), .z_1(u_1), .z_0(u_0));
endmodule

// 4-bit parallel subtractor
module \_4ビット比較器  (
  input  a_3,
  input  a_2,
  input  a_1,
  input  a_0,
  input  b_3,
  input  b_2,
  input  b_1,
  input  b_0,
  output O_F__1,
  output _0_F__2,
  output Result
);

  wire \n4ビット並列減算器_1_u_0 , \n4ビット並列減算器_1_u_1 , \n4ビット並列減算器_1_u_2 , \n4ビット並列減算器_1_u_3 ;

  \_4ビット並列減算器  \u_4ビット並列減算器_1  (
    .s_3(a_3), .s_2(a_2), .s_1(a_1), .s_0(a_0), .t_3(b_3), .t_2(b_2), .t_1(b_1), .t_0(b_0), .O_F__1(O_F__1),
    .O_F__2(_0_F__2), .u_3(\n4ビット並列減算器_1_u_3 ), .u_2(\n4ビット並列減算器_1_u_2 ), .u_1(\n4ビット並列減算器_1_u_1 ),
    .u_0(\n4ビット並列減算器_1_u_0 ));
  nor nor_1 (Result, \n4ビット並列減算器_1_u_3 , \n4ビット並列減算器_1_u_2 , \n4ビット並列減算器_1_u_1 , \n4ビット並列減算器_1_u_0 );
endmodule

module \SRラッチ回路  (
  input  S,
  input  R,
  output Q,
  output Q_prime
);

  wire not_1_out, not_2_out;

  not not_1 (not_1_out, S);
  not not_2 (not_2_out, R);
  nand nand_1 (Q, not_1_out, Q_prime);
  nand nand_2 (Q_prime, Q, not_2_out);
endmodule

// SR-F.F.
module \SRフリップフロップ回路  (
  input  Set,
  input  S,
  input  CLK,
  input  R,
  input  Reset,
  output Q,
  output Q_prime
);

  wire nand_1_out, nand_2_out, not_1_out, not_2_out;

  not not_1 (not_1_out, Set);
  nand nand_1 (nand_1_out, S, CLK);
  nand nand_2 (nand_2_out, CLK, R);
  not not_2 (not_2_out, Reset);
  nand nand_3 (Q, not_1_out, nand_1_out, Q_prime);
  nand nand_4 (Q_prime, Q, nand_2_out, not_2_out);
endmodule

module \JKフリップフロップ回路  (
  input  Set,
  input  J,
  input  CLK,
  input  K,
  input  Reset,
  output Q,
  output Q_prime
);

  wire and_1_out, and_2_out;

  and and_1 (and_1_out, Q_prime, J);
  and and_2 (and_2_out, K, Q);
  \SRフリップフロップ回路  \srフリップフロップ回路_1  (
    .S(and_1_out), .CLK(CLK), .R(and_2_out), .Q(Q), .Q_prime(Q_prime), .Set(Set), .Reset(Reset));
endmodule

// JK-F.F.
module \マスタスレーブJKフリップフロップ回路  (
  input  Set,
  input  J,
  input  K,
  input  CLK,
  input  Reset,
  output Q,
  output Q_prime
);

  wire nand_1_out, nand_2_out, nand_3_out, nand_4_out, nand_5_out, nand_6_out, not_1_out, not_2_out,
       not_3_out;

  not not_1 (not_1_out, Set);
  nand nand_1 (nand_1_out, J, Q_prime, CLK);
  nand nand_2 (nand_2_out, CLK, Q, K);
  not not_2 (not_2_out, Reset);
  nand nand_3 (nand_3_out, not_1_out, nand_1_out, nand_4_out);
  nand nand_4 (nand_4_out, nand_3_out, nand_2_out, not_2_out);
  not not_3 (not_3_out, CLK);
  nand nand_5 (nand_5_out, nand_3_out, not_3_out);
  nand nand_6 (nand_6_out, not_3_out, nand_4_out);
  nand nand_7 (Q, not_1_out, Q_prime, nand_5_out);
  nand nand_8 (Q_prime, nand_6_out, Q, not_2_out);
endmodule

// D-F.F.
module \Dフリップフロップ回路  (
  input  Set,
  input  D,
  input  CLK,
  input  Reset,
  output Q,
  output Q_prime
);

  wire not_1_out;

  not not_1 (not_1_out, D);
  \マスタスレーブJKフリップフロップ回路  \u_マスタスレーブjkフリップフロップ回路_1  (
    .J(D), .K(not_1_out), .CLK(CLK), .Q(Q), .Q_prime(Q_prime), .Set(Set), .Reset(Reset));
endmodule

// Selecter
module _2_bit_selecter (
  input  Select,
  input  X0,
  input  X1,
  output Y
);

  wire and_1_out, and_2_out, not_1_out;

  and and_1 (and_1_out, X0, not_1_out);
  not not_1 (not_1_out, Select);
  and and_2 (and_2_out, X1, Select);
  or or_1 (Y, and_1_out, and_2_out);
endmodule

// 4bit sift regester
module \シフト機能つき4_ビットレジスタ  (
  input  D3,
  input  D2,
  input  D1,
  input  D0,
  input  Set,
  input  Select,
  input  D,
  input  Reset,
  input  CLK,
  output Q3,
  output Q2,
  output Q1,
  output Q0
);

  wire n2_bit_selecter_1_y, n2_bit_selecter_2_y, n2_bit_selecter_3_y, n2_bit_selecter_4_y;

  _2_bit_selecter u_2_bit_selecter_1 (.X0(D), .X1(D3), .Y(n2_bit_selecter_1_y), .Select(Select));
  \Dフリップフロップ回路  \dフリップフロップ回路_1  (
    .D(n2_bit_selecter_1_y), .CLK(CLK), .Q(Q3), .Set(Set), .Reset(Reset));  // open: Q_prime
  _2_bit_selecter u_2_bit_selecter_2 (.X0(Q3), .X1(D2), .Y(n2_bit_selecter_2_y), .Select(Select));
  \Dフリップフロップ回路  \dフリップフロップ回路_2  (
    .D(n2_bit_selecter_2_y), .CLK(CLK), .Q(Q2), .Set(Set), .Reset(Reset));  // open: Q_prime
  _2_bit_selecter u_2_bit_selecter_3 (.X0(Q2), .X1(D1), .Y(n2_bit_selecter_3_y), .Select(Select));
  \Dフリップフロップ回路  \dフリップフロップ回路_3  (
    .D(n2_bit_selecter_3_y), .CLK(CLK), .Q(Q1), .Set(Set), .Reset(Reset));  // open: Q_prime
  _2_bit_selecter u_2_bit_selecter_4 (.X0(Q1), .X1(D0), .Y(n2_bit_selecter_4_y), .Select(Select));
  \Dフリップフロップ回路  \dフリップフロップ回路_4  (
    .D(n2_bit_selecter_4_y), .CLK(CLK), .Q(Q0), .Set(Set), .Reset(Reset));  // open: Q_prime
endmodule

module \_4_ビット直列加算器  (
  input  a_0,
  input  a_1,
  input  a_2,
  input  a_3,
  input  D,
  input  b_0,
  input  b_1,
  input  b_2,
  input  b_3,
  input  CLK,
  input  Select,
  input  Set,
  input  Reset
);

  wire \dフリップフロップ回路_1_q , \n1ビット全加算器_1_c_prime , \n1ビット全加算器_1_s ;
  wire [3:0] \シフト機能つき4_ビットレジスタ_1_q0 , \シフト機能つき4_ビットレジスタ_2_q0 ;

  \シフト機能つき4_ビットレジスタ  \u_シフト機能つき4_ビットレジスタ_1  (
    .Set(Set), .Select(Select), .D(\n1ビット全加算器_1_s ), .Reset(Reset), .CLK(CLK), .D3(a_0), .D2(a_1), .D1(a_2),
    .D0(a_3), .Q3(\シフト機能つき4_ビットレジスタ_1_q0 [3]), .Q2(\シフト機能つき4_ビットレジスタ_1_q0 [2]),
    .Q1(\シフト機能つき4_ビットレジスタ_1_q0 [1]), .Q0(\シフト機能つき4_ビットレジスタ_1_q0 [0]));
  \シフト機能つき4_ビットレジスタ  \u_シフト機能つき4_ビットレジスタ_2  (
    .Set(Set), .Select(Select), .D(D), .Reset(Reset), .CLK(CLK), .D3(b_0), .D2(b_1), .D1(b_2), .D0(b_3),
    .Q3(\シフト機能つき4_ビットレジスタ_2_q0 [3]), .Q2(\シフト機能つき4_ビットレジスタ_2_q0 [2]), .Q1(\シフト機能つき4_ビットレジスタ_2_q0 [1]),
    .Q0(\シフト機能つき4_ビットレジスタ_2_q0 [0]));
  \_1ビット全加算器  \u_1ビット全加算器_1  (
    .A(\シフト機能つき4_ビットレジスタ_1_q0 [0]), .B(\シフト機能つき4_ビットレジスタ_2_q0 [0]), .C(\dフリップフロップ回路_1_q ),
    .C_prime(\n1ビット全加算器_1_c_prime ), .S(\n1ビット全加算器_1_s ));
  \Dフリップフロップ回路  \dフリップフロップ回路_1  (
    .D(\n1ビット全加算器_1_c_prime ), .CLK(CLK), .Q(\dフリップフロップ回路_1_q ), .Set(Set), .Reset(Reset));  // open: Q_prime
  Hex_Digit_Display hex_digit_display_1 (.value(\シフト機能つき4_ビットレジスタ_1_q0 ));  // open: dp
  Hex_Digit_Display hex_digit_display_2 (.value(\シフト機能つき4_ビットレジスタ_2_q0 ));  // open: dp
endmodule

module \乗算回路  (
  input  X_0,
  input  X_1,
  input  Y_0,
  input  Y_1,
  output Z_0,
  output Z_1,
  output Z_2,
  output Z_3
);

  wire and_2_out, and_3_out, and_4_out, \n1ビット半加算器_1_c ;

  and and_1 (Z_0, X_0, Y_0);
  and and_2 (and_2_out, X_1, Y_0);
  and and_3 (and_3_out, X_0, Y_1);
  and and_4 (and_4_out, X_1, Y_1);
  \_1ビット半加算器  \u_1ビット半加算器_1  (.A(and_2_out), .C(\n1ビット半加算器_1_c ), .B(and_3_out), .S(Z_1));
  \_1ビット半加算器  \u_1ビット半加算器_2  (.A(\n1ビット半加算器_1_c ), .C(Z_3), .B(and_4_out), .S(Z_2));
endmodule
